# Fritzing sketch Happyplant  (saved by Fritzing 0.9.3b)
breadboards: 1

parts:
  Part1 = Ethernet Pro
  Part2 = Soil Moisture Sensor
  Part3 = LED Matrix - Serial Interface - Red/Green/Blue

nets:
  N1: Part1.AD0, Part2.SIG
  N2: Part1.*CS, Part3.SCK
  N3: Part1.MOSI, Part3.CS
  N4: Part1.MISO, Part3.MISO
  VCC: Part1.5V, Part2.VCC, Part3.VCC
  GND: Part1.GND, Part2.GND, Part3.GND

notes:
  2-DIN > 12
  3-CS > 11
  4-CLK > 13
  5- VCC> + V5
  1-Ground
  2- VCC> + V5
  3- A0> REDBOARD pin A0
